// Logisim project LALU_2.0.circ as structural Verilog: 9 circuits, main circuit main
module main (
  input  bclk,
  input  rst,
  input  run,
  input  [3:0] dispReg,
  input  dispCyc,
  input  dispIR,
  input  dispPC
);

  wire add, adderOvfl, altiJmp, altJmp, and_2_out, and_4_out, and_5_out, and_6_out, and_7_out, and_8_out,
       and_9_out, and_10_out, and_11_out, and_13_out, and_14_out, and_15_out, and_16_out, and_17_out,
       and_18_out, and_19_out, and_20_out, and_21_out, and_22_out, and_23_out, and_24_out, and_25_out,
       and_26_out, and_27_out, and_28_out, and_29_out, and_30_out, and_31_out, and_32_out, and_33_out,
       and_34_out, and_35_out, and_36_out, and_37_out, and_38_out, and_39_out, and_40_out, and_41_out,
       and_42_out, and_43_out, and_44_out, and_45_out, and_46_out, and_47_out, and_48_out, and_49_out,
       and_50_out, and_51_out, and_53_out, and_56_out, and_57_out, and_59_out, and_60_out, and_61_out,
       and_62_out, and_63_out, and_64_out, and_65_out, and_66_out, any, bAnd, bOr, bs, bsl, bsOob, bsRot,
       bXor, call, callExec, clk, clk_out, cycleCounter_1_oclk, d_ff_1_q, d_ff_1_qn, d_ff_2_qn, d_ff_3_q,
       d_ff_4_q, d_ff_5_q, d_ff_6_q, d_ff_6_qn, dataFlags_1_neg, dataFlags_1_nz, dataFlags_1_zero,
       dataFlags_2_neg, dataFlags_2_odd, dataFlags_2_zero, enpr, exJmp, expr, frozen, fv, halt, hsb, iFlag,
       iJmp, isSignedMul, jmp, jmpAbs, jmpPC, ld, lfm, lfmz, mapOut, memOp, mul, mulOvfl, multiplexer_1_out,
       multiplexer_9_out, mv, not_1_out, or_1_out, or_2_out, or_3_out, or_5_out, or_6_out, or_8_out,
       or_9_out, or_10_out, or_11_out, or_14_out, or_15_out, or_16_out, or_17_out, or_18_out, or_19_out,
       or_21_out, or_23_out, or_24_out, or_25_out, or_26_out, ovfl, par, pipeClk, pop, popIR, prext, prhdl,
       prmem, prprg, prreg, push, register_1_q, register_25_q, register_27_q, ret, retExec, safeClk, sar, st,
       sub, unfl, useAdder, usm, usmz, utilFlag, we;
  wire [0:0] or_20_out;
  wire [2:0] jmpFlags;
  wire [3:0] multiplexer_12_out, multiplexer_12_out_2, multiplexer_12_out_3, multiplexer_12_out_4, Rd, Rj, Rs;
  wire [6:0] multiplexer_19_out;
  wire [6:6] multiplexer_16_out;
  wire [7:0] altImmJmp;
  wire [8:0] dataIn, immJmp;
  wire [15:0] adder_1_out, adder_2_out, adder_3_out, and_58_out, bitShift_1_shifted, cycles, data, dataRd,
       dataRj, dataRs, earlyStackPtr, highestSetBit_1_hsb, IR, ldData, logisim16A_S_1_s, mul16_1_ab,
       multiplexer_2_out, multiplexer_3_out, multiplexer_4_out, multiplexer_5_out, multiplexer_6_out,
       multiplexer_7_out, multiplexer_8_out, multiplexer_10_out, multiplexer_11_out, multiplexer_14_out,
       multiplexer_15_out, multiplexer_20_out, multiplexer_21_out, multiplexer_23_out, multiplexer_25_out,
       multiplexer_26_out, multiplexer_27_out, multiplexer_28_out, multiplexer_29_out, multiplexer_30_out,
       multiplexer_31_out, multiplexer_32_out, multiplexer_33_out, multiplexer_34_out, multiplexer_35_out,
       multiplexer_36_out, multiplexer_38_out, multiplexer_39_out, multiplexer_40_out, multiplexer_41_out,
       multiplexer_43_out, multiplexer_44_out, not_2_out, not_3_out, opc, or_22_out, PC, prExtLoc, prHdlLoc,
       RAM_1_dout, Rdisp, register_2_q, register_5_q, register_6_q, register_7_q, register_8_q, register_9_q,
       register_10_q, register_11_q, register_12_q, register_13_q, register_14_q, register_15_q,
       register_16_q, register_17_q, register_18_q, register_19_q, register_20_q, register_23_q, retVal,
       stackLen, stackPtr, subtractor_1_out, xor_1_out;

  Register #(.width(1)) register_1 (.D(1'b1), .en(halt), .clk(clk), .Q(register_1_q), .clr(rst));
  Clock u_clk (.out(clk_out));
  Multiplexer multiplexer_1 (.in0(bclk), .in1(clk_out), .out(multiplexer_1_out), .sel(run));
  LED clkLED (.in(clk));
  and and_1 (clk, ~register_1_q, d_ff_1_q, multiplexer_1_out);  // AND_Gate
  D_Flip_Flop d_ff_1 (.D(1'b1), .clk(multiplexer_1_out), .Q(d_ff_1_q), .Qn(d_ff_1_qn), .reset(rst));  // open: preset
  LED pipeClkLED (.in(pipeClk));
  Multiplexer #(.width(16)) multiplexer_2 (.in0(PC), .in1(stackLen), .out(multiplexer_2_out), .sel(frozen));
  or or_1 (or_1_out, stackLen[0], stackLen[1], stackLen[2], stackLen[3], stackLen[4], stackLen[5], stackLen[6], stackLen[7], stackLen[8], stackLen[9], stackLen[10], stackLen[11], stackLen[12], stackLen[13], stackLen[14], stackLen[15]);
  or or_2 (or_2_out, jmpAbs, call, enpr);
  cycleCounter cycleCounter_1 (.clk(pipeClk), .rst(rst), .cycles(cycles), .fv(fv), .oClk(cycleCounter_1_oclk));
  and and_2 (and_2_out, retExec, frozen);
  Multiplexer #(.width(16)) multiplexer_3 (.in0(dataRs), .in1(earlyStackPtr), .out(multiplexer_3_out), .sel(pop));
  or or_3 (or_3_out, retExec, pop, ld);
  Multiplexer #(.width(16)) multiplexer_4 (
    .in0(dataRd), .in1(multiplexer_2_out), .out(multiplexer_4_out), .sel(callExec));
  or or_4 (useAdder, add, sub);
  and and_3 (pop, popIR, or_1_out);
  dataFlags dataFlags_2 (
    .data(data), .odd(dataFlags_2_odd), .zero(dataFlags_2_zero), .neg(dataFlags_2_neg));  // open: nz
  Multiplexer #(.width(16)) multiplexer_5 (.in0(dataRj), .in1(retVal), .out(multiplexer_5_out), .sel(ret));
  LED cycClkLED (.in(cycleCounter_1_oclk));
  Multiplexer #(.width(16)) multiplexer_6 (.in0(stackPtr), .in1(adder_1_out), .out(multiplexer_6_out), .sel(and_2_out));
  or or_5 (or_5_out, retExec, and_2_out, callExec, push);
  Multiplexer #(.width(16)) multiplexer_7 (
    .in0(multiplexer_3_out), .in1(multiplexer_6_out), .out(multiplexer_7_out), .sel(or_5_out));
  or or_6 (or_6_out, callExec, push, st);
  Multiplexer #(.width(16)) multiplexer_8 (.in0(multiplexer_4_out), .in1(dataRs), .out(multiplexer_8_out), .sel(push));
  Register #(.width(16)) register_2 (.D(data), .clk(safeClk), .Q(register_2_q), .clr(rst));  // open: en
  Adder #(.width(16)) adder_1 (.a(stackPtr), .b(16'h2), .out(adder_1_out));  // open: cin, cout
  or or_7 (memOp, or_3_out, or_6_out);
  RAM #(.addrWidth(16), .dataWidth(16), .trigger("falling")) RAM_2 (
    .addr(multiplexer_7_out), .we(or_6_out), .oe(or_3_out), .clk(clk), .din(multiplexer_8_out), .dout(ldData));
  or or_8 (or_8_out, bs, mv, ld, bAnd, any, useAdder, bXor, bOr, lfm, lfmz, mul, pop);
  and and_4 (and_4_out, ~jmpFlags[0], ~jmpFlags[1], ~jmpFlags[2]);  // AND_Gate
  and and_5 (and_5_out, dataFlags_2_neg, jmpFlags[0], ~jmpFlags[1], ~jmpFlags[2]);  // AND_Gate
  and and_6 (and_6_out, dataFlags_2_zero, ~jmpFlags[0], jmpFlags[1], ~jmpFlags[2]);  // AND_Gate
  and and_7 (and_7_out, ovfl, jmpFlags[0], jmpFlags[1], ~jmpFlags[2]);  // AND_Gate
  and and_8 (and_8_out, unfl, ~jmpFlags[0], ~jmpFlags[1], jmpFlags[2]);  // AND_Gate
  and and_9 (and_9_out, dataFlags_2_odd, jmpFlags[0], ~jmpFlags[1], jmpFlags[2]);  // AND_Gate
  and and_10 (and_10_out, utilFlag, ~jmpFlags[0], jmpFlags[1], jmpFlags[2]);  // AND_Gate
  and and_11 (and_11_out, ~utilFlag, jmpFlags[0], jmpFlags[1], jmpFlags[2]);  // AND_Gate
  programCounter programCounter_1 (
    .jmpVal(multiplexer_5_out), .jmp(jmpPC), .jmpAbs(or_2_out), .clk(pipeClk), .rst(rst), .pc(opc));
  or or_9 (or_9_out, d_ff_1_qn, pipeClk);
  and and_12 (we, fv, or_8_out);
  Register #(.width(16)) register_3 (.D(opc), .clk(pipeClk), .Q(PC), .clr(rst));  // open: en
  RAM #(.addrWidth(16), .dataWidth(16), .trigger("falling")) RAM_1 (
    .addr(opc), .we(1'b0), .oe(1'b1), .clk(or_9_out), .dout(RAM_1_dout));  // open: din
  dataFlags dataFlags_1 (
    .data(register_2_q), .nz(dataFlags_1_nz), .zero(dataFlags_1_zero), .neg(dataFlags_1_neg));  // open: odd
  Multiplexer multiplexer_9 (.in0(dataFlags_1_nz), .in1(dataFlags_1_zero), .out(multiplexer_9_out), .sel(or_10_out));
  or or_10 (or_10_out, lfmz, usmz);
  and and_13 (and_13_out, jmp, or_11_out);
  or or_11 (or_11_out, and_4_out, and_5_out, and_6_out, and_7_out, and_8_out, and_9_out, and_10_out, and_11_out);
  and and_14 (and_14_out, dataRs[3], multiplexer_9_out);
  or or_12 (jmpPC, call, and_13_out, ret, enpr);
  Multiplexer #(.width(16)) multiplexer_10 (.in0(Rdisp), .in1(cycles), .out(multiplexer_10_out), .sel(dispCyc));
  and and_15 (and_15_out, dataRs[2], dataFlags_1_neg);
  and and_16 (and_16_out, dataRs[1], ovfl);
  Hex_Digit_Display #(.decimalPoint("false")) c3 (.value(multiplexer_12_out_4));
  Multiplexer #(.width(16)) multiplexer_11 (.in0(multiplexer_10_out), .in1(IR), .out(multiplexer_11_out), .sel(dispIR));
  Register #(.trigger("falling"), .width(16)) register_4 (.D(RAM_1_dout), .en(1'b1), .clk(pipeClk), .Q(IR), .clr(rst));
  and and_17 (and_17_out, dataRs[0], unfl);
  Hex_Digit_Display #(.decimalPoint("false")) c2 (.value(multiplexer_12_out_3));
  Hex_Digit_Display #(.decimalPoint("false")) c1 (.value(multiplexer_12_out_2));
  IRDecoder IRDecoder_1 (
    .clk(pipeClk), .rst(rst), .IR(IR), .dataIn(dataIn), .Rs(Rs), .Rd(Rd), .i(iFlag), .add(add), .sub(sub),
    .ld(ld), .mv(mv), .st(st), .halt(halt), .bs(bs), .bsLeft(bsl), .bsRot(bsRot), .bAnd(bAnd), .bOr(bOr),
    .bXor(bXor), .any(any), .lfm(lfm), .lfmz(lfmz), .usm(usm), .usmz(usmz), .hsb(hsb), .exJmp(exJmp),
    .call(callExec), .ret(retExec), .isSignedMul(isSignedMul), .mul(mul), .push(push), .pop(popIR),
    .prreg(prreg), .prmem(prmem), .prprg(prprg));  // open: nop
  Hex_Digit_Display #(.decimalPoint("false")) c0 (.value(multiplexer_12_out));
  Multiplexer #(.width(16)) multiplexer_12 (
    .in0(multiplexer_11_out), .in1(opc),
    .out({multiplexer_12_out_4, multiplexer_12_out_3, multiplexer_12_out_2, multiplexer_12_out}), .sel(dispPC));
  or or_13 (mapOut, and_14_out, and_15_out, and_16_out, and_17_out);
  jumpDecoder jumpDecoder_1 (
    .IR(IR), .flags(jmpFlags), .absolute(jmpAbs), .jmp(jmp), .i(iJmp), .Rj(Rj), .immediate(immJmp),
    .alti(altiJmp), .altImm(altImmJmp), .call(call), .ret(ret), .prext(prext), .prhdl(prhdl),
    .altJmp(altJmp), .enpr(enpr), .expr(expr), .sar(sar), .par(par));
  and and_18 (and_18_out, ~Rd[0], ~Rd[1], ~Rd[2], ~Rd[3]);  // AND_Gate
  and and_19 (and_19_out, Rd[0], ~Rd[1], ~Rd[2], ~Rd[3]);  // AND_Gate
  and and_20 (and_20_out, ~Rd[0], Rd[1], ~Rd[2], ~Rd[3]);  // AND_Gate
  and and_21 (and_21_out, Rd[0], Rd[1], ~Rd[2], ~Rd[3]);  // AND_Gate
  and and_22 (and_22_out, ~Rd[0], ~Rd[1], Rd[2], ~Rd[3]);  // AND_Gate
  and and_23 (and_23_out, Rd[0], ~Rd[1], Rd[2], ~Rd[3]);  // AND_Gate
  and and_24 (and_24_out, ~Rd[0], Rd[1], Rd[2], ~Rd[3]);  // AND_Gate
  and and_25 (and_25_out, Rd[0], Rd[1], Rd[2], ~Rd[3]);  // AND_Gate
  and and_26 (and_26_out, ~Rd[0], ~Rd[1], ~Rd[2], Rd[3]);  // AND_Gate
  and and_27 (and_27_out, Rd[0], ~Rd[1], ~Rd[2], Rd[3]);  // AND_Gate
  and and_28 (and_28_out, ~Rd[0], Rd[1], ~Rd[2], Rd[3]);  // AND_Gate
  and and_29 (and_29_out, Rd[0], Rd[1], ~Rd[2], Rd[3]);  // AND_Gate
  and and_30 (and_30_out, ~Rd[0], ~Rd[1], Rd[2], Rd[3]);  // AND_Gate
  and and_31 (and_31_out, Rd[0], ~Rd[1], Rd[2], Rd[3]);  // AND_Gate
  and and_32 (and_32_out, ~Rd[0], Rd[1], Rd[2], Rd[3]);  // AND_Gate
  and and_33 (and_33_out, Rd[0], Rd[1], Rd[2], Rd[3]);
  Register #(.width(16)) register_5 (.D(data), .en(and_34_out), .clk(pipeClk), .Q(register_5_q), .clr(rst));
  and and_34 (and_34_out, and_18_out, we);
  Register #(.width(16)) register_6 (.D(data), .en(and_35_out), .clk(pipeClk), .Q(register_6_q), .clr(rst));
  and and_35 (and_35_out, and_19_out, we);
  Register #(.width(16)) register_7 (.D(data), .en(and_36_out), .clk(pipeClk), .Q(register_7_q), .clr(rst));
  and and_36 (and_36_out, and_20_out, we);
  Register #(.width(16)) register_8 (.D(data), .en(and_37_out), .clk(pipeClk), .Q(register_8_q), .clr(rst));
  and and_37 (and_37_out, and_21_out, we);
  Register #(.width(16)) register_9 (.D(data), .en(and_38_out), .clk(pipeClk), .Q(register_9_q), .clr(rst));
  and and_38 (and_38_out, and_22_out, we);
  Register #(.width(16)) register_10 (.D(data), .en(and_39_out), .clk(pipeClk), .Q(register_10_q), .clr(rst));
  and and_39 (and_39_out, and_23_out, we);
  Register #(.width(16)) register_11 (.D(data), .en(and_40_out), .clk(pipeClk), .Q(register_11_q), .clr(rst));
  and and_40 (and_40_out, and_24_out, we);
  Register #(.width(16)) register_12 (.D(data), .en(and_41_out), .clk(pipeClk), .Q(register_12_q), .clr(rst));
  and and_41 (and_41_out, and_25_out, we);
  Register #(.width(16)) register_13 (.D(data), .en(and_42_out), .clk(pipeClk), .Q(register_13_q), .clr(rst));
  and and_42 (and_42_out, and_26_out, we);
  Register #(.width(16)) register_14 (.D(data), .en(and_43_out), .clk(pipeClk), .Q(register_14_q), .clr(rst));
  and and_43 (and_43_out, and_27_out, we);
  Register #(.width(16)) register_15 (.D(data), .en(and_44_out), .clk(pipeClk), .Q(register_15_q), .clr(rst));
  and and_44 (and_44_out, and_28_out, we);
  Register #(.width(16)) register_16 (.D(data), .en(and_45_out), .clk(pipeClk), .Q(register_16_q), .clr(rst));
  and and_45 (and_45_out, and_29_out, we);
  Register #(.width(16)) register_17 (.D(data), .en(and_46_out), .clk(pipeClk), .Q(register_17_q), .clr(rst));
  and and_46 (and_46_out, and_30_out, we);
  Register #(.width(16)) register_18 (.D(data), .en(and_47_out), .clk(pipeClk), .Q(register_18_q), .clr(rst));
  and and_47 (and_47_out, and_31_out, we);
  Register #(.width(16)) register_19 (.D(data), .en(and_48_out), .clk(pipeClk), .Q(register_19_q), .clr(rst));
  and and_48 (and_48_out, and_32_out, we);
  Register #(.width(16)) register_20 (.D(data), .en(and_49_out), .clk(pipeClk), .Q(register_20_q), .clr(rst));
  and and_49 (and_49_out, and_33_out, we);
  Multiplexer #(.select(4), .width(16)) multiplexer_13 (
    .in0(register_5_q), .in1(register_6_q), .in2(register_7_q), .in3(register_8_q), .in4(register_9_q),
    .in5(register_10_q), .in6(register_11_q), .in7(register_12_q), .in8(register_13_q), .in9(register_14_q),
    .in10(register_15_q), .in11(register_16_q), .in12(register_17_q), .in13(register_18_q),
    .in14(register_19_q), .in15(register_20_q), .out(dataRd), .sel(Rd));
  Multiplexer #(.select(4), .width(16)) multiplexer_14 (
    .in0(register_5_q), .in1(register_6_q), .in2(register_7_q), .in3(register_8_q), .in4(register_9_q),
    .in5(register_10_q), .in6(register_11_q), .in7(register_12_q), .in8(register_13_q), .in9(register_14_q),
    .in10(register_15_q), .in11(register_16_q), .in12(register_17_q), .in13(register_18_q),
    .in14(register_19_q), .in15(register_20_q), .out(multiplexer_14_out), .sel(Rs));
  Multiplexer #(.select(4), .width(16)) multiplexer_15 (
    .in0(register_5_q), .in1(register_6_q), .in2(register_7_q), .in3(register_8_q), .in4(register_9_q),
    .in5(register_10_q), .in6(register_11_q), .in7(register_12_q), .in8(register_13_q), .in9(register_14_q),
    .in10(register_15_q), .in11(register_16_q), .in12(register_17_q), .in13(register_18_q),
    .in14(register_19_q), .in15(register_20_q), .out(multiplexer_15_out), .sel(Rj));
  Multiplexer multiplexer_16 (.in0(immJmp[8]), .in1(1'b0), .out(multiplexer_16_out[6]), .sel(jmpAbs));
  Multiplexer #(.select(4), .width(16)) multiplexer_17 (
    .in0(register_5_q), .in1(register_6_q), .in2(register_7_q), .in3(register_8_q), .in4(register_9_q),
    .in5(register_10_q), .in6(register_11_q), .in7(register_12_q), .in8(register_13_q), .in9(register_14_q),
    .in10(register_15_q), .in11(register_16_q), .in12(register_17_q), .in13(register_18_q),
    .in14(register_19_q), .in15(register_20_q), .out(Rdisp), .sel(dispReg));
  Multiplexer #(.width(16)) multiplexer_18 (
    .in0(multiplexer_14_out), .in1({{12{1'b0}}, Rs}), .out(dataRs), .sel(iFlag));
  Multiplexer #(.width(7)) multiplexer_19 (
    .in0({7{multiplexer_16_out[6]}}), .in1(dataIn[6:0]), .out(multiplexer_19_out), .sel(exJmp));
  Multiplexer #(.width(16)) multiplexer_20 (
    .in0(multiplexer_15_out), .in1({multiplexer_19_out, immJmp}), .out(multiplexer_20_out), .sel(or_14_out));
  or or_14 (or_14_out, iJmp, call);
  logisim16A_S logisim16A_S_1 (.a(dataRd), .b(dataRs), .OP(sub), .s(logisim16A_S_1_s), .overflow(adderOvfl));
  D_Flip_Flop d_ff_2 (.D(d_ff_5_q), .clk(clk), .Qn(d_ff_2_qn), .reset(not_1_out));  // open: Q, preset
  Register #(.width(16)) register_21 (.D(dataRj), .en(prext), .clk(safeClk), .Q(prExtLoc), .clr(rst));
  or or_15 (or_15_out, usm, usmz);
  D_Flip_Flop d_ff_3 (.D(and_50_out), .clk(safeClk), .Q(d_ff_3_q), .reset(rst));  // open: Qn, preset
  and and_50 (and_50_out, d_ff_6_qn, or_16_out);
  or or_16 (or_16_out, call, ret);
  and and_51 (and_51_out, memOp, d_ff_2_qn);
  not not_1 (not_1_out, and_51_out);
  Multiplexer #(.width(16)) multiplexer_21 (
    .in0(logisim16A_S_1_s), .in1(ldData), .out(multiplexer_21_out), .sel(or_17_out));
  or or_17 (or_17_out, pop, ld);
  D_Flip_Flop d_ff_4 (.D(utilFlag), .clk(safeClk), .Q(d_ff_4_q), .reset(rst));  // open: Qn, preset
  Multiplexer multiplexer_22 (.in0(d_ff_4_q), .in1(mapOut), .out(utilFlag), .sel(or_15_out));
  Multiplexer #(.width(16)) multiplexer_23 (
    .in0(multiplexer_15_out), .in1({dataIn[7:0], altImmJmp}), .out(multiplexer_23_out), .sel(altiJmp));
  and and_52 (safeClk, clk, ~and_51_out);  // AND_Gate
  D_Flip_Flop d_ff_5 (.D(and_51_out), .clk(clk), .Q(d_ff_5_q), .reset(not_1_out));  // open: Qn, preset
  Multiplexer #(.width(16)) multiplexer_24 (
    .in0(multiplexer_20_out), .in1(multiplexer_23_out), .out(dataRj), .sel(altJmp));
  or or_18 (or_18_out, and_50_out, d_ff_3_q);
  D_Flip_Flop d_ff_6 (.D(or_18_out), .clk(safeClk), .Q(d_ff_6_q), .Qn(d_ff_6_qn), .reset(rst));  // open: preset
  assign not_2_out = ~stackLen;  // NOT_Gate not_2, 16 bits wide
  and and_53 (and_53_out, retExec, ~frozen);  // AND_Gate
  Register #(.width(16)) register_22 (.D(dataRj), .en(prhdl), .clk(safeClk), .Q(prHdlLoc), .clr(rst));
  Multiplexer #(.width(16)) multiplexer_25 (.in0(multiplexer_21_out), .in1(dataRs), .out(multiplexer_25_out), .sel(mv));
  Multiplexer #(.width(16)) multiplexer_26 (.in0(16'h1), .in1({16{1'b1}}), .out(multiplexer_26_out), .sel(pop));
  Multiplexer #(.width(16)) multiplexer_27 (
    .in0(multiplexer_26_out), .in1(not_2_out), .out(multiplexer_27_out), .sel(ret));
  and and_54 (frozen, ~d_ff_3_q, d_ff_6_q);  // AND_Gate
  bitShift bitShift_1 (
    .rot(bsRot), .left(bsl), .data(dataRd), .amt(dataRs[3:0]), .shifted(bitShift_1_shifted), .oob(bsOob));
  assign not_3_out = ~ldData;  // NOT_Gate not_3, 16 bits wide
  Multiplexer #(.width(16)) multiplexer_28 (
    .in0(multiplexer_27_out), .in1(not_3_out), .out(multiplexer_28_out), .sel(and_53_out));
  and and_55 (pipeClk, d_ff_6_qn, safeClk);
  Multiplexer #(.width(16)) multiplexer_29 (
    .in0(multiplexer_25_out), .in1(bitShift_1_shifted), .out(multiplexer_29_out), .sel(bs));
  Multiplexer #(.width(16)) multiplexer_30 (
    .in0(multiplexer_28_out), .in1(stackLen), .out(multiplexer_30_out), .sel(and_56_out));
  and and_56 (and_56_out, ~and_53_out, retExec);  // AND_Gate
  Adder #(.width(16)) adder_2 (.a(register_23_q), .b(multiplexer_30_out), .out(adder_2_out));  // open: cin, cout
  Register #(.width(16)) register_23 (.D(adder_2_out), .en(or_19_out), .clk(safeClk), .Q(register_23_q), .clr(rst));
  or or_19 (or_19_out, pop, ret, retExec, callExec, push);
  and and_57 (and_57_out, frozen, retExec);
  Multiplexer #(.width(16)) multiplexer_31 (
    .in0(multiplexer_29_out), .in1(and_58_out), .out(multiplexer_31_out), .sel(bAnd));
  assign and_58_out = dataRd & dataRs;  // AND_Gate and_58, 16 bits wide
  Multiplexer #(.width(16)) multiplexer_32 (
    .in0(multiplexer_36_out), .in1(xor_1_out), .out(multiplexer_32_out), .sel(bXor));
  assign xor_1_out = dataRd ^ dataRs;  // XOR_Gate xor_1, 16 bits wide
  Subtractor #(.width(16)) subtractor_1 (.a(register_23_q), .b(16'h1), .out(subtractor_1_out));  // open: bin, bout
  or or_20 (or_20_out[0], dataRs[15], dataRs[14], dataRs[13], dataRs[12], dataRs[11], dataRs[10], dataRs[9], dataRs[8], dataRs[7], dataRs[6], dataRs[5], dataRs[4], dataRs[3], dataRs[2], dataRs[1], dataRs[0]);
  Multiplexer #(.width(16)) multiplexer_33 (
    .in0(adder_2_out), .in1(subtractor_1_out), .out(multiplexer_33_out), .sel(and_59_out));
  and and_59 (and_59_out, ret, pop);
  assign stackPtr = ~register_23_q;  // NOT_Gate not_4, 16 bits wide
  Multiplexer #(.width(16)) multiplexer_34 (.in0(PC), .in1(ldData), .out(multiplexer_34_out), .sel(and_57_out));
  Register #(.width(16)) register_24 (.D(multiplexer_34_out), .en(or_21_out), .clk(safeClk), .Q(retVal), .clr(rst));
  or or_21 (or_21_out, and_57_out, callExec);
  assign or_22_out = dataRd | dataRs;  // OR_Gate or_22, 16 bits wide
  Multiplexer #(.width(16)) multiplexer_35 (
    .in0(multiplexer_32_out), .in1({{15{1'b0}}, or_20_out[0]}), .out(multiplexer_35_out), .sel(any));
  assign earlyStackPtr = ~multiplexer_33_out;  // NOT_Gate not_5, 16 bits wide
  Multiplexer #(.width(16)) multiplexer_36 (
    .in0(multiplexer_31_out), .in1(or_22_out), .out(multiplexer_36_out), .sel(bOr));
  and and_60 (and_60_out, mulOvfl, mul);
  and and_61 (and_61_out, adderOvfl, useAdder);
  and and_62 (and_62_out, bsOob, bsl, bs);
  Multiplexer multiplexer_37 (.in0(register_25_q), .in1(or_23_out), .out(ovfl), .sel(or_24_out));
  Register #(.width(1)) register_25 (.D(or_23_out), .en(or_24_out), .clk(safeClk), .Q(register_25_q), .clr(rst));
  or or_23 (or_23_out, and_60_out, and_61_out, and_62_out);
  or or_24 (or_24_out, bs, mul, useAdder);
  Multiplexer #(.width(16)) multiplexer_38 (.in0(16'h1), .in1({16{1'b1}}), .out(multiplexer_38_out), .sel(pop));
  and and_63 (and_63_out, ~frozen, retExec);  // AND_Gate
  Multiplexer #(.width(16)) multiplexer_39 (
    .in0(multiplexer_35_out), .in1({{15{1'b0}}, mapOut}), .out(multiplexer_39_out), .sel(or_25_out));
  or or_25 (or_25_out, lfm, lfmz);
  LED u_ovfl (.in(register_25_q));
  Adder #(.width(16)) adder_3 (.a(stackLen), .b(multiplexer_38_out), .out(adder_3_out));  // open: cin, cout
  Multiplexer #(.width(16)) multiplexer_40 (
    .in0(adder_3_out), .in1(ldData), .out(multiplexer_40_out), .sel(and_63_out));
  Multiplexer #(.width(16)) multiplexer_41 (
    .in0(multiplexer_40_out), .in1({16{1'b0}}), .out(multiplexer_41_out), .sel(and_64_out));
  or or_26 (or_26_out, push, pop, and_63_out, and_64_out);
  and and_64 (and_64_out, frozen, callExec);
  Register #(.width(16)) register_26 (.D(multiplexer_41_out), .en(or_26_out), .clk(safeClk), .Q(stackLen), .clr(rst));
  Multiplexer multiplexer_42 (.in0(register_27_q), .in1(and_65_out), .out(unfl), .sel(bs));
  Register #(.width(1)) register_27 (.D(and_65_out), .en(bs), .clk(safeClk), .Q(register_27_q), .clr(rst));
  and and_65 (and_65_out, bsOob, ~bsl, bs);  // AND_Gate
  highestSetBit highestSetBit_1 (.data(dataRd), .hsb(highestSetBit_1_hsb));
  Multiplexer #(.width(16)) multiplexer_43 (
    .in0(multiplexer_39_out), .in1(highestSetBit_1_hsb), .out(multiplexer_43_out), .sel(hsb));
  mul16 mul16_1 (.A(dataRd), .B(dataRs), .s(isSignedMul), .AB(mul16_1_ab), .O(mulOvfl));
  Multiplexer #(.width(16)) multiplexer_44 (
    .in0(multiplexer_43_out), .in1(mul16_1_ab), .out(multiplexer_44_out), .sel(mul));
  Multiplexer #(.width(16)) multiplexer_45 (.in0(multiplexer_44_out), .in1({16{1'b0}}), .out(data), .sel(and_66_out));
  and and_66 (and_66_out, ~pop, popIR);  // AND_Gate

  // Notes on the sheet:
  //   Inputs
  //   Cycle Counter
  //   Data Memory
  //   Instruction Flags
  //   Jump Logic
  //   Program Loader
  //   IR Handling
  //   Flag Map
  //   Hex Display
  //   Register Control
  //   Data Handling
  //   Prot Exit Loc
  //   Freeze Pipeline
  //   Util Register
  //   Prot Handle Loc
  //   Stack Pointer
  //   Current Return Address
  //   Overflow/Underflow
  //   Stack Length
endmodule

module programCounter (
  input  [15:0] jmpVal,
  input  jmp,
  input  jmpAbs,
  input  clk,
  input  rst,
  output [15:0] pc
);

  wire and_1_out, and_2_out;
  wire [15:0] adder_1_out, multiplexer_1_out, multiplexer_2_out, multiplexer_3_out, register_2_q;

  Multiplexer #(.width(16)) multiplexer_1 (.in0(16'h1), .in1(jmpVal), .out(multiplexer_1_out), .sel(and_1_out));
  and and_1 (and_1_out, jmp, ~jmpAbs);  // AND_Gate
  Multiplexer #(.width(16)) multiplexer_2 (.in0(pc), .in1(register_2_q), .out(multiplexer_2_out), .sel(and_1_out));
  Adder #(.width(16)) adder_1 (.a(multiplexer_2_out), .b(multiplexer_1_out), .out(adder_1_out));  // open: cin, cout
  and and_2 (and_2_out, jmp, jmpAbs);
  Register #(.width(16)) register_1 (.D(multiplexer_3_out), .clk(clk), .Q(pc), .clr(rst));  // open: en
  Multiplexer #(.width(16)) multiplexer_3 (.in0(adder_1_out), .in1(jmpVal), .out(multiplexer_3_out), .sel(and_2_out));
  Register #(.width(16)) register_2 (.D(pc), .clk(clk), .Q(register_2_q), .clr(rst));  // open: en
endmodule

module cycleCounter (
  input  clk,
  input  rst,
  output [15:0] cycles,
  output fv,
  output oClk
);

  wire [15:0] adder_1_out;

  Adder #(.width(16)) adder_1 (.a(cycles), .b(16'h1), .out(adder_1_out));  // open: cin, cout
  Register #(.width(16)) register_1 (.D(adder_1_out), .en(1'b1), .clk(clk), .Q(cycles), .clr(rst));
  Register #(.width(1)) register_2 (.D(1'b1), .en(adder_1_out[1]), .clk(clk), .Q(fv), .clr(rst));

  assign oClk = clk;
endmodule

module jumpDecoder (
  input  [15:0] IR,
  output [2:0] flags,
  output absolute,
  output jmp,
  output i,
  output [3:0] Rj,
  output [8:0] immediate,
  output alti,
  output [7:0] altImm,
  output call,
  output ret,
  output prext,
  output prhdl,
  output altJmp,
  output enpr,
  output expr,
  output sar,
  output par
);

  and and_1 (call, ~IR[0], ~IR[1], IR[2], ~IR[3], IR[4], ~IR[5], ~IR[6]);  // AND_Gate
  and and_2 (ret, IR[0], ~IR[1], IR[2], ~IR[3], IR[4], ~IR[5], ~IR[6]);  // AND_Gate
  and and_3 (prext, IR[0], IR[1], ~IR[2], ~IR[3], ~IR[4], IR[5], ~IR[6]);  // AND_Gate
  and and_4 (prhdl, ~IR[0], ~IR[1], IR[2], ~IR[3], ~IR[4], IR[5], ~IR[6]);  // AND_Gate
  and and_5 (enpr, IR[0], ~IR[1], IR[2], ~IR[3], ~IR[4], IR[5], ~IR[6]);  // AND_Gate
  and and_6 (expr, ~IR[0], IR[1], IR[2], ~IR[3], ~IR[4], IR[5], ~IR[6]);  // AND_Gate
  and and_7 (sar, IR[0], IR[1], IR[2], ~IR[3], ~IR[4], IR[5], ~IR[6]);  // AND_Gate
  and and_8 (par, ~IR[0], ~IR[1], ~IR[2], IR[3], ~IR[4], IR[5], ~IR[6]);  // AND_Gate
  and and_9 (jmp, ~IR[5], IR[6]);  // AND_Gate
  or or_1 (altJmp, prext, prhdl, enpr);

  assign absolute = IR[4];
  assign alti = IR[7];
  assign altImm = IR[15:8];
  assign flags = IR[2:0];
  assign i = IR[3];
  assign immediate = IR[15:7];
  assign Rj = IR[10:7];
endmodule

module IRDecoder (
  input  clk,
  input  rst,
  input  [15:0] IR,
  output [8:0] dataIn,
  output [3:0] Rs,
  output [3:0] Rd,
  output i,
  output nop,
  output add,
  output sub,
  output ld,
  output mv,
  output st,
  output halt,
  output bs,
  output bsLeft,
  output bsRot,
  output bAnd,
  output bOr,
  output bXor,
  output any,
  output lfm,
  output lfmz,
  output usm,
  output usmz,
  output hsb,
  output exJmp,
  output call,
  output ret,
  output isSignedMul,
  output mul,
  output push,
  output pop,
  output prreg,
  output prmem,
  output prprg
);

  wire and_1_out, and_2_out, and_3_out, and_4_out, and_5_out, and_6_out, and_7_out, and_8_out, and_9_out,
       and_10_out, and_11_out, and_12_out, and_13_out, and_14_out, and_15_out, and_16_out, and_17_out,
       and_18_out, and_19_out, and_20_out, and_21_out, and_22_out, and_23_out, and_24_out, and_25_out,
       and_26_out;

  Register #(.width(9)) register_1 (.D(IR[15:7]), .clk(clk), .Q(dataIn), .clr(rst));  // open: en
  Register #(.width(4)) register_2 (.D(IR[11:8]), .clk(clk), .Q(Rs), .clr(rst));  // open: en
  Register #(.width(4)) register_3 (.D(IR[15:12]), .clk(clk), .Q(Rd), .clr(rst));  // open: en
  D_Flip_Flop d_ff_1 (.D(IR[7]), .clk(clk), .Q(i), .reset(rst));  // open: Qn, preset
  and and_1 (and_1_out, ~IR[0], ~IR[1], ~IR[2], ~IR[3], ~IR[4], ~IR[5], ~IR[6]);  // AND_Gate
  and and_2 (and_2_out, IR[0], ~IR[1], ~IR[2], ~IR[3], ~IR[4], ~IR[5], ~IR[6]);  // AND_Gate
  and and_3 (and_3_out, ~IR[0], IR[1], ~IR[2], ~IR[3], ~IR[4], ~IR[5], ~IR[6]);  // AND_Gate
  and and_4 (and_4_out, IR[0], IR[1], ~IR[2], ~IR[3], ~IR[4], ~IR[5], ~IR[6]);  // AND_Gate
  and and_5 (and_5_out, ~IR[0], ~IR[1], IR[2], ~IR[3], ~IR[4], ~IR[5], ~IR[6]);  // AND_Gate
  and and_6 (and_6_out, IR[0], ~IR[1], IR[2], ~IR[3], ~IR[4], ~IR[5], ~IR[6]);  // AND_Gate
  and and_7 (and_7_out, IR[0], IR[1], IR[2], IR[3], IR[4], IR[5], IR[6]);
  and and_8 (and_8_out, IR[2], IR[3], ~IR[4], ~IR[5], ~IR[6]);  // AND_Gate
  and and_9 (and_9_out, ~IR[0], ~IR[1], ~IR[2], ~IR[3], IR[4], ~IR[5], ~IR[6]);  // AND_Gate
  and and_10 (and_10_out, IR[0], ~IR[1], ~IR[2], ~IR[3], IR[4], ~IR[5], ~IR[6]);  // AND_Gate
  and and_11 (and_11_out, ~IR[0], IR[1], ~IR[2], ~IR[3], IR[4], ~IR[5], ~IR[6]);  // AND_Gate
  and and_12 (and_12_out, IR[0], IR[1], ~IR[2], ~IR[3], IR[4], ~IR[5], ~IR[6]);  // AND_Gate
  and and_13 (and_13_out, ~IR[0], IR[1], IR[2], ~IR[3], IR[4], ~IR[5], ~IR[6]);  // AND_Gate
  and and_14 (and_14_out, ~IR[0], IR[1], ~IR[2], IR[3], IR[4], ~IR[5], ~IR[6]);  // AND_Gate
  and and_15 (and_15_out, IR[0], IR[1], IR[2], ~IR[3], IR[4], ~IR[5], ~IR[6]);  // AND_Gate
  and and_16 (and_16_out, ~IR[0], ~IR[1], ~IR[2], IR[3], IR[4], ~IR[5], ~IR[6]);  // AND_Gate
  and and_17 (and_17_out, IR[0], IR[1], ~IR[2], IR[3], IR[4], ~IR[5], ~IR[6]);  // AND_Gate
  and and_18 (and_18_out, ~IR[0], IR[1], IR[2], IR[3], IR[4], ~IR[5], ~IR[6]);  // AND_Gate
  and and_19 (and_19_out, ~IR[0], ~IR[1], IR[2], ~IR[3], IR[4], ~IR[5], ~IR[6]);  // AND_Gate
  and and_20 (and_20_out, IR[0], ~IR[1], IR[2], ~IR[3], IR[4], ~IR[5], ~IR[6]);  // AND_Gate
  and and_21 (and_21_out, IR[1], IR[2], ~IR[3], ~IR[4], ~IR[5], ~IR[6]);  // AND_Gate
  and and_22 (and_22_out, ~IR[0], ~IR[1], ~IR[2], IR[3], ~IR[4], ~IR[5], ~IR[6]);  // AND_Gate
  and and_23 (and_23_out, IR[0], ~IR[1], ~IR[2], IR[3], ~IR[4], ~IR[5], ~IR[6]);  // AND_Gate
  and and_24 (and_24_out, ~IR[0], ~IR[1], ~IR[2], ~IR[3], ~IR[4], IR[5], ~IR[6]);  // AND_Gate
  and and_25 (and_25_out, IR[0], ~IR[1], ~IR[2], ~IR[3], ~IR[4], IR[5], ~IR[6]);  // AND_Gate
  and and_26 (and_26_out, ~IR[0], IR[1], ~IR[2], ~IR[3], ~IR[4], IR[5], ~IR[6]);  // AND_Gate
  D_Flip_Flop d_ff_2 (.D(and_1_out), .clk(clk), .Q(nop), .reset(rst));  // open: Qn, preset
  D_Flip_Flop d_ff_3 (.D(and_2_out), .clk(clk), .Q(add), .reset(rst));  // open: Qn, preset
  D_Flip_Flop d_ff_4 (.D(and_3_out), .clk(clk), .Q(sub), .reset(rst));  // open: Qn, preset
  D_Flip_Flop d_ff_5 (.D(and_4_out), .clk(clk), .Q(ld), .reset(rst));  // open: Qn, preset
  D_Flip_Flop d_ff_6 (.D(and_5_out), .clk(clk), .Q(mv), .reset(rst));  // open: Qn, preset
  D_Flip_Flop d_ff_7 (.D(and_6_out), .clk(clk), .Q(st), .reset(rst));  // open: Qn, preset
  D_Flip_Flop d_ff_8 (.D(and_7_out), .clk(clk), .Q(halt), .reset(rst));  // open: Qn, preset
  D_Flip_Flop d_ff_9 (.D(and_8_out), .clk(clk), .Q(bs), .reset(rst));  // open: Qn, preset
  D_Flip_Flop d_ff_10 (.D(IR[0]), .clk(clk), .Qn(bsLeft), .reset(rst));  // open: Q, preset
  D_Flip_Flop d_ff_11 (.D(IR[1]), .clk(clk), .Q(bsRot), .reset(rst));  // open: Qn, preset
  D_Flip_Flop d_ff_12 (.D(and_9_out), .clk(clk), .Q(bAnd), .reset(rst));  // open: Qn, preset
  D_Flip_Flop d_ff_13 (.D(and_10_out), .clk(clk), .Q(bOr), .reset(rst));  // open: Qn, preset
  D_Flip_Flop d_ff_14 (.D(and_11_out), .clk(clk), .Q(bXor), .reset(rst));  // open: Qn, preset
  D_Flip_Flop d_ff_15 (.D(and_12_out), .clk(clk), .Q(any), .reset(rst));  // open: Qn, preset
  D_Flip_Flop d_ff_16 (.D(and_13_out), .clk(clk), .Q(lfm), .reset(rst));  // open: Qn, preset
  D_Flip_Flop d_ff_17 (.D(and_14_out), .clk(clk), .Q(lfmz), .reset(rst));  // open: Qn, preset
  D_Flip_Flop d_ff_18 (.D(and_15_out), .clk(clk), .Q(usm), .reset(rst));  // open: Qn, preset
  D_Flip_Flop d_ff_19 (.D(and_16_out), .clk(clk), .Q(usmz), .reset(rst));  // open: Qn, preset
  D_Flip_Flop d_ff_20 (.D(and_17_out), .clk(clk), .Q(hsb), .reset(rst));  // open: Qn, preset
  D_Flip_Flop d_ff_21 (.D(and_18_out), .clk(clk), .Q(exJmp), .reset(rst));  // open: Qn, preset
  D_Flip_Flop d_ff_22 (.D(and_19_out), .clk(clk), .Q(call), .reset(rst));  // open: Qn, preset
  D_Flip_Flop d_ff_23 (.D(and_20_out), .clk(clk), .Q(ret), .reset(rst));  // open: Qn, preset
  D_Flip_Flop d_ff_24 (.D(IR[0]), .clk(clk), .Qn(isSignedMul), .reset(rst));  // open: Q, preset
  D_Flip_Flop d_ff_25 (.D(and_21_out), .clk(clk), .Q(mul), .reset(rst));  // open: Qn, preset
  D_Flip_Flop d_ff_26 (.D(and_22_out), .clk(clk), .Q(push), .reset(rst));  // open: Qn, preset
  D_Flip_Flop d_ff_27 (.D(and_23_out), .clk(clk), .Q(pop), .reset(rst));  // open: Qn, preset
  D_Flip_Flop d_ff_28 (.D(and_24_out), .clk(clk), .Q(prreg), .reset(rst));  // open: Qn, preset
  D_Flip_Flop d_ff_29 (.D(and_25_out), .clk(clk), .Q(prmem), .reset(rst));  // open: Qn, preset
  D_Flip_Flop d_ff_30 (.D(and_26_out), .clk(clk), .Q(prprg), .reset(rst));  // open: Qn, preset
endmodule

module bitShift (
  input  rot,
  input  left,
  input  [15:0] data,
  input  [3:0] amt,
  output [15:0] shifted,
  output oob
);

  wire a, b, c, d, e, f, g, h, i, j, k, l, la, lb, lc, ld, le, lf, lg, lh, li, lj, lk, ll, lm, ln, lo, lp, m,
       multiplexer_5_out, multiplexer_6_out, multiplexer_9_out, multiplexer_11_out, multiplexer_13_out,
       multiplexer_14_out, multiplexer_17_out, multiplexer_19_out, multiplexer_21_out, multiplexer_22_out,
       multiplexer_25_out, multiplexer_27_out, multiplexer_29_out, multiplexer_30_out, multiplexer_33_out, n,
       o, p;
  wire [15:0] multiplexer_2_out, reverse16_1_output_bus_1, reverse16_2_output_bus_1;

  and and_1 (la, a, rot);
  and and_2 (lb, b, rot);
  and and_3 (lc, c, rot);
  and and_4 (ld, d, rot);
  and and_5 (le, e, rot);
  and and_6 (lf, f, rot);
  and and_7 (lg, g, rot);
  and and_8 (lh, h, rot);
  and and_9 (li, i, rot);
  and and_10 (lj, j, rot);
  and and_11 (lk, k, rot);
  and and_12 (ll, l, rot);
  and and_13 (lm, m, rot);
  and and_14 (ln, n, rot);
  and and_15 (lo, o, rot);
  and and_16 (lp, p, rot);
  Multiplexer #(.width(16)) multiplexer_1 (
    .in0(multiplexer_2_out), .in1(reverse16_2_output_bus_1), .out(shifted), .sel(left));
  reverse16 reverse16_2 (.Input_bus_1(multiplexer_2_out), .Output_bus_1(reverse16_2_output_bus_1));
  or or_1 (oob, multiplexer_5_out, multiplexer_6_out, multiplexer_9_out, multiplexer_11_out, multiplexer_13_out, multiplexer_14_out, multiplexer_17_out, multiplexer_19_out, multiplexer_21_out, multiplexer_22_out, multiplexer_25_out, multiplexer_27_out, multiplexer_29_out, multiplexer_30_out, multiplexer_33_out);
  Multiplexer #(.select(4)) multiplexer_2 (
    .in0(a), .in1(b), .in2(c), .in3(d), .in4(e), .in5(f), .in6(g), .in7(h), .in8(i), .in9(j), .in10(k),
    .in11(l), .in12(m), .in13(n), .in14(o), .in15(p), .out(multiplexer_2_out[0]), .sel(amt));
  reverse16 reverse16_1 (.Input_bus_1(data), .Output_bus_1(reverse16_1_output_bus_1));
  Multiplexer #(.width(16)) multiplexer_3 (
    .in0(data), .in1(reverse16_1_output_bus_1), .out({p, o, n, m, l, k, j, i, h, g, f, e, d, c, b, a}),
    .sel(left));
  Multiplexer #(.select(4)) multiplexer_4 (
    .in0(b), .in1(c), .in2(d), .in3(e), .in4(f), .in5(g), .in6(h), .in7(i), .in8(j), .in9(j), .in10(l),
    .in11(m), .in12(n), .in13(o), .in14(p), .in15(la), .out(multiplexer_2_out[1]), .sel(amt));
  Multiplexer #(.select(4)) multiplexer_5 (
    .in0(1'b0), .in1(1'b0), .in2(1'b0), .in3(1'b0), .in4(1'b0), .in5(1'b0), .in6(1'b0), .in7(1'b0),
    .in8(1'b0), .in9(1'b0), .in10(1'b0), .in11(1'b0), .in12(1'b0), .in13(1'b0), .in14(1'b0), .in15(a),
    .out(multiplexer_5_out), .sel(amt));
  Multiplexer #(.select(4)) multiplexer_6 (
    .in0(1'b0), .in1(1'b0), .in2(1'b0), .in3(1'b0), .in4(1'b0), .in5(1'b0), .in6(1'b0), .in7(1'b0),
    .in8(1'b0), .in9(1'b0), .in10(1'b0), .in11(1'b0), .in12(1'b0), .in13(1'b0), .in14(a), .in15(b),
    .out(multiplexer_6_out), .sel(amt));
  Multiplexer #(.select(4)) multiplexer_7 (
    .in0(c), .in1(d), .in2(e), .in3(f), .in4(g), .in5(h), .in6(i), .in7(j), .in8(k), .in9(l), .in10(m),
    .in11(n), .in12(o), .in13(p), .in14(la), .in15(lb), .out(multiplexer_2_out[2]), .sel(amt));
  Multiplexer #(.select(4)) multiplexer_8 (
    .in0(d), .in1(e), .in2(f), .in3(g), .in4(h), .in5(i), .in6(j), .in7(k), .in8(l), .in9(m), .in10(n),
    .in11(o), .in12(p), .in13(la), .in14(lb), .in15(lc), .out(multiplexer_2_out[3]), .sel(amt));
  Multiplexer #(.select(4)) multiplexer_9 (
    .in0(1'b0), .in1(1'b0), .in2(1'b0), .in3(1'b0), .in4(1'b0), .in5(1'b0), .in6(1'b0), .in7(1'b0),
    .in8(1'b0), .in9(1'b0), .in10(1'b0), .in11(1'b0), .in12(1'b0), .in13(a), .in14(b), .in15(c),
    .out(multiplexer_9_out), .sel(amt));
  Multiplexer #(.select(4)) multiplexer_10 (
    .in0(e), .in1(f), .in2(g), .in3(h), .in4(i), .in5(j), .in6(k), .in7(l), .in8(m), .in9(n), .in10(o),
    .in11(p), .in12(la), .in13(lb), .in14(lc), .in15(ld), .out(multiplexer_2_out[4]), .sel(amt));
  Multiplexer #(.select(4)) multiplexer_11 (
    .in0(1'b0), .in1(1'b0), .in2(1'b0), .in3(1'b0), .in4(1'b0), .in5(1'b0), .in6(1'b0), .in7(1'b0),
    .in8(1'b0), .in9(1'b0), .in10(1'b0), .in11(1'b0), .in12(a), .in13(b), .in14(c), .in15(d),
    .out(multiplexer_11_out), .sel(amt));
  Multiplexer #(.select(4)) multiplexer_12 (
    .in0(f), .in1(g), .in2(h), .in3(i), .in4(j), .in5(k), .in6(l), .in7(m), .in8(n), .in9(o), .in10(p),
    .in11(la), .in12(lb), .in13(lc), .in14(ld), .in15(le), .out(multiplexer_2_out[5]), .sel(amt));
  Multiplexer #(.select(4)) multiplexer_13 (
    .in0(1'b0), .in1(1'b0), .in2(1'b0), .in3(1'b0), .in4(1'b0), .in5(1'b0), .in6(1'b0), .in7(1'b0),
    .in8(1'b0), .in9(1'b0), .in10(1'b0), .in11(a), .in12(b), .in13(c), .in14(d), .in15(e),
    .out(multiplexer_13_out), .sel(amt));
  Multiplexer #(.select(4)) multiplexer_14 (
    .in0(1'b0), .in1(1'b0), .in2(1'b0), .in3(1'b0), .in4(1'b0), .in5(1'b0), .in6(1'b0), .in7(1'b0),
    .in8(1'b0), .in9(1'b0), .in10(a), .in11(b), .in12(c), .in13(d), .in14(e), .in15(f),
    .out(multiplexer_14_out), .sel(amt));
  Multiplexer #(.select(4)) multiplexer_15 (
    .in0(g), .in1(h), .in2(i), .in3(j), .in4(k), .in5(l), .in6(m), .in7(n), .in8(o), .in9(p), .in10(la),
    .in11(lb), .in12(lc), .in13(ld), .in14(le), .in15(lf), .out(multiplexer_2_out[6]), .sel(amt));
  Multiplexer #(.select(4)) multiplexer_16 (
    .in0(h), .in1(i), .in2(j), .in3(k), .in4(l), .in5(m), .in6(n), .in7(o), .in8(p), .in9(la), .in10(lb),
    .in11(lc), .in12(ld), .in13(le), .in14(lf), .in15(lg), .out(multiplexer_2_out[7]), .sel(amt));
  Multiplexer #(.select(4)) multiplexer_17 (
    .in0(1'b0), .in1(1'b0), .in2(1'b0), .in3(1'b0), .in4(1'b0), .in5(1'b0), .in6(1'b0), .in7(1'b0),
    .in8(1'b0), .in9(a), .in10(b), .in11(c), .in12(d), .in13(e), .in14(f), .in15(g),
    .out(multiplexer_17_out), .sel(amt));
  Multiplexer #(.select(4)) multiplexer_18 (
    .in0(i), .in1(j), .in2(k), .in3(l), .in4(m), .in5(n), .in6(o), .in7(p), .in8(la), .in9(lb), .in10(lc),
    .in11(ld), .in12(le), .in13(lf), .in14(lg), .in15(lh), .out(multiplexer_2_out[8]), .sel(amt));
  Multiplexer #(.select(4)) multiplexer_19 (
    .in0(1'b0), .in1(1'b0), .in2(1'b0), .in3(1'b0), .in4(1'b0), .in5(1'b0), .in6(1'b0), .in7(1'b0), .in8(a),
    .in9(b), .in10(c), .in11(d), .in12(e), .in13(f), .in14(g), .in15(h), .out(multiplexer_19_out), .sel(amt));
  Multiplexer #(.select(4)) multiplexer_20 (
    .in0(j), .in1(k), .in2(l), .in3(m), .in4(n), .in5(o), .in6(p), .in7(la), .in8(lb), .in9(lc), .in10(ld),
    .in11(le), .in12(lf), .in13(lg), .in14(lh), .in15(li), .out(multiplexer_2_out[9]), .sel(amt));
  Multiplexer #(.select(4)) multiplexer_21 (
    .in0(1'b0), .in1(1'b0), .in2(1'b0), .in3(1'b0), .in4(1'b0), .in5(1'b0), .in6(1'b0), .in7(a), .in8(b),
    .in9(c), .in10(d), .in11(e), .in12(f), .in13(g), .in14(h), .in15(i), .out(multiplexer_21_out), .sel(amt));
  Multiplexer #(.select(4)) multiplexer_22 (
    .in0(1'b0), .in1(1'b0), .in2(1'b0), .in3(1'b0), .in4(1'b0), .in5(1'b0), .in6(a), .in7(b), .in8(c),
    .in9(d), .in10(e), .in11(f), .in12(g), .in13(h), .in14(i), .in15(j), .out(multiplexer_22_out), .sel(amt));
  Multiplexer #(.select(4)) multiplexer_23 (
    .in0(k), .in1(l), .in2(m), .in3(n), .in4(o), .in5(p), .in6(la), .in7(lb), .in8(lc), .in9(ld), .in10(le),
    .in11(lf), .in12(lg), .in13(lh), .in14(li), .in15(lj), .out(multiplexer_2_out[10]), .sel(amt));
  Multiplexer #(.select(4)) multiplexer_24 (
    .in0(l), .in1(m), .in2(n), .in3(o), .in4(p), .in5(la), .in6(lb), .in7(lc), .in8(ld), .in9(le), .in10(lf),
    .in11(lg), .in12(lh), .in13(li), .in14(lj), .in15(lk), .out(multiplexer_2_out[11]), .sel(amt));
  Multiplexer #(.select(4)) multiplexer_25 (
    .in0(1'b0), .in1(1'b0), .in2(1'b0), .in3(1'b0), .in4(1'b0), .in5(a), .in6(b), .in7(c), .in8(d), .in9(e),
    .in10(f), .in11(g), .in12(h), .in13(i), .in14(j), .in15(k), .out(multiplexer_25_out), .sel(amt));
  Multiplexer #(.select(4)) multiplexer_26 (
    .in0(m), .in1(n), .in2(o), .in3(p), .in4(la), .in5(lb), .in6(lc), .in7(ld), .in8(le), .in9(lf),
    .in10(lg), .in11(lh), .in12(li), .in13(lj), .in14(lk), .in15(ll), .out(multiplexer_2_out[12]), .sel(amt));
  Multiplexer #(.select(4)) multiplexer_27 (
    .in0(1'b0), .in1(1'b0), .in2(1'b0), .in3(1'b0), .in4(a), .in5(b), .in6(c), .in7(d), .in8(e), .in9(f),
    .in10(g), .in11(h), .in12(i), .in13(j), .in14(k), .in15(l), .out(multiplexer_27_out), .sel(amt));
  Multiplexer #(.select(4)) multiplexer_28 (
    .in0(n), .in1(o), .in2(p), .in3(la), .in4(lb), .in5(lc), .in6(ld), .in7(le), .in8(lf), .in9(lg),
    .in10(lh), .in11(li), .in12(lj), .in13(lk), .in14(ll), .in15(lm), .out(multiplexer_2_out[13]), .sel(amt));
  Multiplexer #(.select(4)) multiplexer_29 (
    .in0(1'b0), .in1(1'b0), .in2(1'b0), .in3(a), .in4(b), .in5(c), .in6(d), .in7(e), .in8(f), .in9(g),
    .in10(h), .in11(i), .in12(j), .in13(k), .in14(l), .in15(m), .out(multiplexer_29_out), .sel(amt));
  Multiplexer #(.select(4)) multiplexer_30 (
    .in0(1'b0), .in1(1'b0), .in2(a), .in3(b), .in4(c), .in5(d), .in6(e), .in7(f), .in8(g), .in9(h), .in10(i),
    .in11(j), .in12(k), .in13(l), .in14(m), .in15(n), .out(multiplexer_30_out), .sel(amt));
  Multiplexer #(.select(4)) multiplexer_31 (
    .in0(o), .in1(p), .in2(la), .in3(lb), .in4(lc), .in5(ld), .in6(le), .in7(lf), .in8(lg), .in9(lh),
    .in10(li), .in11(lj), .in12(lk), .in13(ll), .in14(lm), .in15(ln), .out(multiplexer_2_out[14]), .sel(amt));
  Multiplexer #(.select(4)) multiplexer_32 (
    .in0(p), .in1(la), .in2(lb), .in3(lc), .in4(ld), .in5(le), .in6(lf), .in7(lg), .in8(lh), .in9(li),
    .in10(lj), .in11(lk), .in12(ll), .in13(lm), .in14(ln), .in15(lo), .out(multiplexer_2_out[15]), .sel(amt));
  Multiplexer #(.select(4)) multiplexer_33 (
    .in0(1'b0), .in1(a), .in2(b), .in3(c), .in4(d), .in5(e), .in6(f), .in7(g), .in8(h), .in9(i), .in10(j),
    .in11(k), .in12(l), .in13(m), .in14(n), .in15(o), .out(multiplexer_33_out), .sel(amt));

  // Other names for the same wires on the sheet: x[3:0] = amt
endmodule

module reverse16 (
  input  [15:0] Input_bus_1,
  output [15:0] Output_bus_1
);


  assign Output_bus_1 = {Input_bus_1[0], Input_bus_1[1], Input_bus_1[2], Input_bus_1[3], Input_bus_1[4], Input_bus_1[5], Input_bus_1[6], Input_bus_1[7], Input_bus_1[8], Input_bus_1[9], Input_bus_1[10], Input_bus_1[11], Input_bus_1[12], Input_bus_1[13], Input_bus_1[14], Input_bus_1[15]};
endmodule

module dataFlags (
  input  [15:0] data,
  output odd,
  output nz,
  output zero,
  output neg
);

  nor nor_1 (zero, data[0], data[1], data[2], data[3], data[4], data[5], data[6], data[7], data[8], data[9], data[10], data[11], data[12], data[13], data[14], data[15]);
  not not_1 (nz, zero);

  assign neg = data[15];
  assign odd = data[0];
endmodule

module highestSetBit (
  input  [15:0] data,
  output [15:0] hsb
);

  wire [15:0] multiplexer_1_out, multiplexer_2_out, multiplexer_3_out, multiplexer_4_out, multiplexer_5_out,
       multiplexer_6_out, multiplexer_7_out, multiplexer_8_out, multiplexer_9_out, multiplexer_10_out,
       multiplexer_11_out, multiplexer_12_out, multiplexer_13_out, multiplexer_14_out, multiplexer_15_out;

  Multiplexer #(.width(16)) multiplexer_1 (.in0({16{1'b0}}), .in1(16'h1), .out(multiplexer_1_out), .sel(data[0]));
  Multiplexer #(.width(16)) multiplexer_2 (
    .in0(multiplexer_1_out), .in1(16'h2), .out(multiplexer_2_out), .sel(data[1]));
  Multiplexer #(.width(16)) multiplexer_3 (
    .in0(multiplexer_2_out), .in1(16'h4), .out(multiplexer_3_out), .sel(data[2]));
  Multiplexer #(.width(16)) multiplexer_4 (
    .in0(multiplexer_3_out), .in1(16'h8), .out(multiplexer_4_out), .sel(data[3]));
  Multiplexer #(.width(16)) multiplexer_5 (
    .in0(multiplexer_4_out), .in1(16'h10), .out(multiplexer_5_out), .sel(data[4]));
  Multiplexer #(.width(16)) multiplexer_6 (
    .in0(multiplexer_5_out), .in1(16'h20), .out(multiplexer_6_out), .sel(data[5]));
  Multiplexer #(.width(16)) multiplexer_7 (
    .in0(multiplexer_6_out), .in1(16'h40), .out(multiplexer_7_out), .sel(data[6]));
  Multiplexer #(.width(16)) multiplexer_8 (
    .in0(multiplexer_7_out), .in1(16'h80), .out(multiplexer_8_out), .sel(data[7]));
  Multiplexer #(.width(16)) multiplexer_9 (
    .in0(multiplexer_8_out), .in1(16'h100), .out(multiplexer_9_out), .sel(data[8]));
  Multiplexer #(.width(16)) multiplexer_10 (
    .in0(multiplexer_9_out), .in1(16'h200), .out(multiplexer_10_out), .sel(data[9]));
  Multiplexer #(.width(16)) multiplexer_11 (
    .in0(multiplexer_10_out), .in1(16'h400), .out(multiplexer_11_out), .sel(data[10]));
  Multiplexer #(.width(16)) multiplexer_12 (
    .in0(multiplexer_11_out), .in1(16'h800), .out(multiplexer_12_out), .sel(data[11]));
  Multiplexer #(.width(16)) multiplexer_13 (
    .in0(multiplexer_12_out), .in1(16'h1000), .out(multiplexer_13_out), .sel(data[12]));
  Multiplexer #(.width(16)) multiplexer_14 (
    .in0(multiplexer_13_out), .in1(16'h2000), .out(multiplexer_14_out), .sel(data[13]));
  Multiplexer #(.width(16)) multiplexer_15 (
    .in0(multiplexer_14_out), .in1(16'h4000), .out(multiplexer_15_out), .sel(data[14]));
  Multiplexer #(.width(16)) multiplexer_16 (.in0(multiplexer_15_out), .in1(16'h8000), .out(hsb), .sel(data[15]));
endmodule
